// Digital circuit RegisterFile_ALU.dig as structural Verilog
module RegisterFile_ALU (
);

  Register_file_4bit register_file_4bit_1 ();  // open: Sel_read1, Sel_read2, clk, Write_data, Sel_write, CTRL_registers, Read_data_1, Read_data_2
  _4_bit_ALU _4_bit_alu_1 ();  // open: A, B, S_1_S_0_C_in, D, overflow
endmodule
